// Logisim project prac1.circ as structural Verilog: 1 circuit, main circuit main
module main (
  input  [2:0] INPC,
  input  [3:0] INPA,
  input  [3:0] INPB,
  input  in_4
);

  wire a, adder_1_cout, BI, BS, clock_1_out, CT, CTI, d_ff_1_q, OS, RG_B_q3, RG_R_out, RLD, RS, rst, TT;
  wire [2:0] counter_1_q;
  wire [3:0] adder_1_out, and_1_out, RG_A_q, RG_O_q3, RG_R_q3, rom_1_data;
  wire [4:0] multiplexer_1_out;

  Clock clock_1 (.out(clock_1_out));
  or or_1 (TT, clock_1_out, in_4);
  Multiplexer multiplexer_1 (.in0(a), .out(multiplexer_1_out[0]), .sel(1'b0));  // open: in1, en
  Counter #(.width(3), .max('h7)) counter_1 (
    .load(1'b1), .D(INPC), .count(CTI), .Q(counter_1_q), .clk(CT), .clr(rst));  // open: carry
  Register #(.width(4)) RG_A (.D(INPA), .Q(RG_A_q), .clk(TT), .clr(rst));  // open: en
  Shift_Register #(.length(4)) RG_B (
    .shift(BS), .in(1'b0), .clk(TT), .load(BI), .clr(rst), .d0(INPB[3]), .d1(INPB[2]), .d2(INPB[1]),
    .d3(INPB[0]), .q3(RG_B_q3));  // open: out, q0, q1, q2
  nor nor_1 (a, counter_1_q[0], counter_1_q[1], counter_1_q[2]);
  Shift_Register #(.length(4)) RG_R (
    .shift(RS), .in(d_ff_1_q), .clk(TT), .out(RG_R_out), .load(RLD), .clr(rst), .d0(adder_1_out[3]),
    .q0(RG_R_q3[3]), .d1(adder_1_out[2]), .q1(RG_R_q3[2]), .d2(adder_1_out[1]), .q2(RG_R_q3[1]),
    .d3(adder_1_out[0]), .q3(RG_R_q3[0]));
  Register #(.width(4)) register_1 (.D(rom_1_data), .Q(multiplexer_1_out[4:1]), .clk(TT));  // open: en, clr
  ROM #(.addrWidth(5), .dataWidth(4)) rom_1 (.addr(multiplexer_1_out), .data(rom_1_data));  // open: sel
  Shift_Register #(.length(4)) RG_O (
    .shift(OS), .in(RG_R_out), .clk(TT), .clr(rst), .q0(RG_O_q3[3]), .q1(RG_O_q3[2]), .q2(RG_O_q3[1]),
    .q3(RG_O_q3[0]));  // open: out, load, d0, d1, d2, d3
  and and_1 (and_1_out[0], RG_A_q[0], RG_B_q3);
  and and_2 (and_1_out[1], RG_A_q[1], RG_B_q3);
  and and_3 (and_1_out[2], RG_A_q[2], RG_B_q3);
  and and_4 (and_1_out[3], RG_A_q[3], RG_B_q3);
  ROM #(.addrWidth(4)) rom_2 (.addr(multiplexer_1_out[4:1]), .data({rst, CTI, CT, BI, RS, OS, RLD, BS}));  // open: sel
  Adder #(.width(4)) adder_1 (.a(RG_R_q3), .b(and_1_out), .out(adder_1_out), .cout(adder_1_cout));  // open: cin
  D_Flip_Flop d_ff_1 (.clk(TT), .D(adder_1_cout), .Q(d_ff_1_q), .reset(rst));  // open: Qn, preset, en

  // Notes on the sheet:
  //   contents of rom_1 (hex, n*v repeats v):
  //   1 1 2 0 3 3 4 4 5 5 2
  //   contents of rom_2 (hex, n*v repeats v):
  //   80 30 2 d 60
endmodule
