// Logisim project prac2.circ as structural Verilog: 1 circuit, main circuit main
module main (
  input  [2:0] in_1,
  input  [4:0] in_2,
  input  [4:0] in_3,
  input  in_4
);

  wire _11, a, and_1_out, and_2_out, and_3_out, and_4_out, and_5_out, b, BL, BS, clock_1_out, CT, CTI,
       d_ff_1_q, inv, multiplexer_1_out, OS, RG_R_out, RLD, RS, rst, TT;
  wire [2:0] cnt_q;
  wire [3:0] multiplexer_2_out, register_1_q, rom_1_data_2;
  wire [4:0] adder_1_out, RG_A_q, RG_O_q4, RG_R_q4, xor_1_out;
  wire [10:0] rom_1_data;

  Shift_Register #(.length(5)) RG_B (
    .shift(BS), .in(1'b0), .clk(TT), .load(BL), .clr(rst), .d0(in_3[4]), .d1(in_3[3]), .d2(in_3[2]),
    .d3(in_3[1]), .d4(in_3[0]), .q4(b));  // open: out, q0, q1, q2, q3
  or or_1 (TT, in_4, clock_1_out);
  Clock clock_1 (.out(clock_1_out));
  D_Flip_Flop d_ff_1 (.clk(TT), .D(_11), .Q(d_ff_1_q));  // open: Qn, preset, en, reset
  Counter #(.width(3), .max('h7)) cnt (
    .load(1'b1), .D(in_1), .count(CTI), .Q(cnt_q), .clk(CT), .clr(rst));  // open: carry
  or or_2 (a, cnt_q[0], cnt_q[1], cnt_q[2]);
  Register #(.width(5)) RG_A (.D(in_2), .Q(RG_A_q), .clk(TT), .clr(rst));  // open: en
  Multiplexer multiplexer_1 (.in0(b), .in1(a), .out(multiplexer_1_out), .sel(rom_1_data[10]));  // open: en
  Multiplexer #(.width(4)) multiplexer_2 (
    .in0(rom_1_data[9:6]), .in1(rom_1_data_2), .out(multiplexer_2_out), .sel(multiplexer_1_out));  // open: en
  Shift_Register #(.length(5)) RG_R (
    .shift(RS), .in(d_ff_1_q), .clk(TT), .out(RG_R_out), .load(RLD), .clr(rst), .d0(adder_1_out[4]),
    .q0(RG_R_q4[4]), .d1(adder_1_out[3]), .q1(RG_R_q4[3]), .d2(adder_1_out[2]), .q2(RG_R_q4[2]),
    .d3(adder_1_out[1]), .q3(RG_R_q4[1]), .d4(adder_1_out[0]), .q4(RG_R_q4[0]));
  Register #(.width(4)) register_1 (.D(multiplexer_2_out), .Q(register_1_q), .clk(TT));  // open: en, clr
  and and_1 (and_1_out, b, RG_A_q[0]);
  and and_2 (and_2_out, b, RG_A_q[1]);
  and and_3 (and_3_out, b, RG_A_q[2]);
  and and_4 (and_4_out, b, RG_A_q[3]);
  and and_5 (and_5_out, b, RG_A_q[4]);
  xor xor_1 (xor_1_out[0], and_1_out, inv);
  xor xor_2 (xor_1_out[1], and_2_out, inv);
  xor xor_3 (xor_1_out[2], and_3_out, inv);
  xor xor_4 (xor_1_out[3], and_4_out, inv);
  xor xor_5 (xor_1_out[4], and_5_out, inv);
  ROM #(.addrWidth(4), .dataWidth(20)) rom_1 (
    .addr(register_1_q),
    .data({rst, CT, CTI, BL, RS, OS, RLD, BS, inv, rom_1_data[10:6], rom_1_data_2, rom_1_data[1:0]}));  // open: sel
  Shift_Register #(.length(5)) RG_O (
    .shift(OS), .in(RG_R_out), .clk(TT), .clr(rst), .q0(RG_O_q4[4]), .q1(RG_O_q4[3]), .q2(RG_O_q4[2]),
    .q3(RG_O_q4[1]), .q4(RG_O_q4[0]));  // open: out, load, d0, d1, d2, d3, d4
  xor xor_6 (_11, inv, RG_A_q[4]);
  Adder #(.width(5)) adder_1 (.a(RG_R_q4), .b(xor_1_out), .out(adder_1_out), .cin(inv));  // open: cout

  // Notes on the sheet:
  //   contents of rom_1 (hex, n*v repeats v):
  //   80044 50220 20cc 6d5d8 2954 c264 c8 150 c8
endmodule
