// Logisim project prac2.circ as structural Verilog: 1 circuit, main circuit main
module main (
);

  Shift_Register #(.length(4)) RG_B (.in(1'b0));  // open: shift, clk, out, load, clr, d0, q0, d1, q1, d2, q2, d3, q3
  Counter #(.width(3), .max('h7)) cnt ();  // open: load, D, count, Q, carry, clk, clr
  Register #(.width(4)) RG_A ();  // open: D, en, Q, clk, clr
  Shift_Register #(.length(4)) RG_R ();  // open: shift, in, clk, out, load, clr, d0, q0, d1, q1, d2, q2, d3, q3
  Shift_Register #(.length(4)) RG_O ();  // open: shift, in, clk, out, load, clr, d0, q0, d1, q1, d2, q2, d3, q3
endmodule
