// Logisim project prac3.circ as structural Verilog: 1 circuit, main circuit main
module main (
  input  [3:0] \Делитель ,
  input  [3:0] \Делимое ,
  input  in_3,
  input  in_4,
  input  in_5,
  input  [7:0] in_6
);

  wire _0_1_2_3_4_2_out, a_t, adder_2_cout, b, c, CHS, CT, CTI, d_ff_1_q, d_ff_2_q, err, inv, not_2_out,
       not_3_out, not_4_out, not_6_out, OLD, OS, RLD, RS, rst;
  wire [0:0] multiplexer_1_out;
  wire [1:0] rom_1_data;
  wire [2:0] counter_2_q, rom_1_data_2;
  wire [3:0] _0_1_2_3_4_3_q0, register_1_q;
  wire [4:0] _0_1_2_3_4_q0, A, adder_1_out, AI, multiplexer_2_out, not_1_out, rez, RG_B_q;
  wire [15:15] rom_1_data_3;

  Counter counter_1 (.load(1'b1), .D(in_6), .count(in_4), .clk(in_5));  // open: Q, carry, clr
  D_Flip_Flop d_ff_1 (.clk(in_3), .D(CTI), .Q(d_ff_1_q));  // open: Qn, preset, en, reset
  assign not_1_out = ~5'b01001;  // NOT_Gate not_1, 5 bits wide
  Counter #(.width(3), .max('h7)) counter_2 (
    .load(1'b1), .D(3'b100), .count(d_ff_1_q), .Q(counter_2_q), .clk(not_2_out), .clr(rst));  // open: carry
  not not_2 (not_2_out, CT);
  Adder #(.width(5)) adder_1 (.a(not_1_out), .b(5'b00001), .out(adder_1_out));  // open: cin, cout
  not not_3 (not_3_out, in_3);
  Register #(.width(5)) RG_B (.D(5'b01000), .Q(RG_B_q), .clk(not_4_out), .clr(rst));  // open: en
  not not_4 (not_4_out, in_3);
  Shift_Register #(.length(5)) _0_1_2_3_4 (
    .shift(RS), .in(_0_1_2_3_4_2_out), .clk(in_3), .load(RLD), .clr(rst), .d0(rez[0]), .q0(_0_1_2_3_4_q0[0]),
    .d1(rez[1]), .q1(_0_1_2_3_4_q0[1]), .d2(rez[2]), .q2(_0_1_2_3_4_q0[2]), .d3(rez[3]),
    .q3(_0_1_2_3_4_q0[3]), .d4(rez[4]), .q4(_0_1_2_3_4_q0[4]));  // open: out
  nor nor_1 (b, counter_2_q[0], counter_2_q[1], counter_2_q[2]);
  Register #(.width(5)) RG_AI (.D(adder_1_out), .Q(AI), .clk(in_3), .clr(rst));  // open: en
  Register #(.width(5)) RG_A (.D(5'b01001), .Q(A), .clk(not_3_out), .clr(rst));  // open: en
  Multiplexer #(.select(2)) multiplexer_1 (
    .in0(rom_1_data_3[15]), .in1(a_t), .in2(b), .in3(c), .out(multiplexer_1_out[0]), .sel(rom_1_data));  // open: en
  not not_5 (a_t, _0_1_2_3_4_q0[4]);
  Register #(.width(4)) register_1 (
    .D({rom_1_data_2, multiplexer_1_out[0]}), .Q(register_1_q), .clk(in_3));  // open: en, clr
  nor nor_2 (c, A[0], A[1], A[2], A[3], A[4]);
  Shift_Register #(.length(5)) _0_1_2_3_4_2 (
    .shift(OS), .in(1'b0), .clk(in_3), .out(_0_1_2_3_4_2_out), .load(d_ff_2_q), .clr(rst), .d0(RG_B_q[0]),
    .d1(RG_B_q[1]), .d2(RG_B_q[2]), .d3(RG_B_q[3]), .d4(RG_B_q[4]));  // open: q0, q1, q2, q3, q4
  ROM #(.addrWidth(4), .dataWidth(16)) rom_1 (
    .addr(register_1_q),
    .data({rom_1_data_3[15], rom_1_data_2, rst, CTI, CT, RS, RLD, OLD, OS, inv, CHS, err, rom_1_data}));  // open: sel
  Shift_Register #(.length(5)) _0_1_2_3_4_3 (
    .shift(CHS), .in(adder_2_cout), .clk(in_3), .clr(rst), .q0(_0_1_2_3_4_3_q0[0]), .q1(_0_1_2_3_4_3_q0[1]),
    .q2(_0_1_2_3_4_3_q0[2]), .q3(_0_1_2_3_4_3_q0[3]));  // open: out, load, d0, d1, d2, d3, d4, q4
  not not_6 (not_6_out, in_3);
  LED led_1 (.in(err));
  D_Flip_Flop d_ff_2 (.clk(not_6_out), .D(OLD), .Q(d_ff_2_q));  // open: Qn, preset, en, reset
  Multiplexer #(.width(5)) multiplexer_2 (.in0(A), .in1(AI), .out(multiplexer_2_out), .sel(inv));  // open: en
  Adder #(.width(5)) adder_2 (.a(multiplexer_2_out), .b(_0_1_2_3_4_q0), .out(rez), .cout(adder_2_cout));  // open: cin

  // Other names for the same wires on the sheet: TT = in_3

  // Notes on the sheet:
  //   contents of rom_1 (hex, n*v repeats v):
  //   8800 1243 2121 4 368a 369a 2121 4001 c080
  //   Частное
endmodule
