// Logisim project prac3.circ as structural Verilog: 1 circuit, main circuit main
module main (
  input  [3:0] \Делитель ,
  input  [3:0] \Делимое 
);

  wire _0_1_2_3_4_2_out, adder_2_cout, CHS, CT, CTI, inv, OLD, OS, RS, RST, TT;
  wire [4:0] _0_1_2_3_4_3_q0, _0_1_2_3_4_q0, A, adder_1_out, AI, multiplexer_2_out, not_1_out, rez, RG_B_q;

  assign not_1_out = ~{1'b0, \Делитель };  // NOT_Gate not_1, 5 bits wide
  Counter #(.width(3), .max('h7)) counter_1 (.D(3'b100), .count(CTI), .clk(CT), .clr(TT));  // open: load, Q, carry
  Adder #(.width(5)) adder_1 (.a(not_1_out), .b(5'b00001), .out(adder_1_out));  // open: cin, cout
  Register #(.width(5)) RG_B (.D({1'b0, \Делимое }), .Q(RG_B_q), .clk(TT), .clr(RST));  // open: en
  Shift_Register #(.length(5)) _0_1_2_3_4 (
    .in(_0_1_2_3_4_2_out), .clk(TT), .load(RS), .clr(RST), .d0(rez[0]), .q0(_0_1_2_3_4_q0[0]), .d1(rez[1]),
    .q1(_0_1_2_3_4_q0[1]), .d2(rez[2]), .q2(_0_1_2_3_4_q0[2]), .d3(rez[3]), .q3(_0_1_2_3_4_q0[3]),
    .d4(rez[4]), .q4(_0_1_2_3_4_q0[4]));  // open: shift, out
  Register #(.width(5)) RG_AI (.D(adder_1_out), .Q(AI), .clk(TT), .clr(RST));  // open: en
  Register #(.width(5)) RG_A (.D({1'b0, \Делитель }), .Q(A), .clk(TT), .clr(RST));  // open: en
  Multiplexer multiplexer_1 ();  // open: in0, in1, out, sel, en
  Register register_1 ();  // open: D, en, Q, clk, clr
  Shift_Register #(.length(5)) _0_1_2_3_4_2 (
    .shift(OS), .in(1'b0), .clk(TT), .out(_0_1_2_3_4_2_out), .load(OLD), .clr(RST), .d0(RG_B_q[0]),
    .d1(RG_B_q[1]), .d2(RG_B_q[2]), .d3(RG_B_q[3]), .d4(RG_B_q[4]));  // open: q0, q1, q2, q3, q4
  ROM rom_1 ();  // open: addr, data, sel
  Shift_Register #(.length(5)) _0_1_2_3_4_3 (
    .shift(CHS), .clk(TT), .clr(RST), .q0(_0_1_2_3_4_3_q0[0]), .q1(_0_1_2_3_4_3_q0[1]),
    .q2(_0_1_2_3_4_3_q0[2]), .q3(_0_1_2_3_4_3_q0[3]), .q4(_0_1_2_3_4_3_q0[4]));  // open: in, out, load, d0, d1, d2, d3, d4
  Multiplexer #(.width(5)) multiplexer_2 (.in0(A), .in1(AI), .out(multiplexer_2_out), .sel(inv));  // open: en
  Adder #(.width(5)) adder_2 (.a(multiplexer_2_out), .b(_0_1_2_3_4_q0), .out(rez), .cout(adder_2_cout));  // open: cin

  // Notes on the sheet:
  //   Частное
endmodule
