// Logisim project 4.circ as structural Verilog: 1 circuit, main circuit main
module main (
);

  wire adder_4_cout, and_1_out, C, CHCK, CT_0, LD_AB, LD_Ost1, LD_Ost1_2, LD_Ost2, multiplexer_1_out,
       not_3_out, not_5_out, R0, RST, SH_B, SH_Out, shift_register_1_out, STEP;
  wire [1:0] lastOp;
  wire [2:0] counter_1_q;
  wire [4:0] adder_2_out, adder_3_out, adder_5_out, adder_6_out, adder_7_out, adder_8_out, Chastnoe,
       ChastnoeOtv, input2, multiplexer_5_out, not_2_out, not_4_out, not_6_out, not_7_out, not_8_out,
       not_9_out, Ost, Ostatok, OstatokOtv, register_2_q, RGR_INP;
  wire [9:0] adder_1_out, input1, not_1_out, register_1_q;
  wire [11:0] multiplexer_2_out, rom_1_data, rom_2_data;

  Button button_1 (.out(C));
  LED led_1 (.in(R0));
  // Probe on 10'h3f3
  // Probe on 5'b00011
  // Probe on ChastnoeOtv
  // Probe on ChastnoeOtv
  // Probe on OstatokOtv
  // Probe on OstatokOtv
  Multiplexer #(.enable("false")) multiplexer_1 (
    .in0(register_1_q[0]), .in1(CT_0), .out(multiplexer_1_out), .sel(register_1_q[9]));
  // Probe on 10'h3f3
  // Probe on 5'b00011
  Shift_Register #(.length(5)) shift_register_1 (
    .shift(SH_Out), .in(not_3_out), .clk(C), .out(shift_register_1_out), .load(LD_AB), .clr(RST),
    .d0(input1[0]), .q0(Chastnoe[0]), .d1(input1[1]), .q1(Chastnoe[1]), .d2(input1[2]), .q2(Chastnoe[2]),
    .d3(input1[3]), .q3(Chastnoe[3]), .d4(input1[4]), .q4(Chastnoe[4]));
  ROM #(.addrWidth(2), .dataWidth(12)) rom_1 (.addr(lastOp), .data(rom_1_data));  // open: sel
  ROM #(.addrWidth(2), .dataWidth(12)) rom_2 (.addr(lastOp), .data(rom_2_data));  // open: sel
  Shift_Register #(.length(5)) shift_register_2 (
    .shift(SH_B), .in(shift_register_1_out), .clk(C), .load(LD_Ost1_2), .clr(RST), .d0(Ost[0]),
    .q0(Ostatok[0]), .d1(Ost[1]), .q1(Ostatok[1]), .d2(Ost[2]), .q2(Ostatok[2]), .d3(Ost[3]),
    .q3(Ostatok[3]), .d4(Ost[4]), .q4(Ostatok[4]));  // open: out
  Multiplexer #(.width(12)) multiplexer_2 (
    .in0(rom_2_data), .in1(rom_1_data), .out(multiplexer_2_out), .sel(multiplexer_1_out));  // open: en
  Register #(.width(12)) register_1 (
    .D(multiplexer_2_out),
    .Q({lastOp, register_1_q[9], SH_Out, CHCK, STEP, SH_B, RST, LD_Ost2, LD_Ost1, LD_AB, register_1_q[0]}),
    .clk(C));  // open: en, clr
  assign not_1_out = ~10'h3f3;  // NOT_Gate not_1, 10 bits wide
  assign not_2_out = ~5'b00011;  // NOT_Gate not_2, 5 bits wide
  not not_3 (not_3_out, adder_4_cout);
  Adder #(.width(10)) adder_1 (.a(not_1_out), .b(10'h1), .out(adder_1_out));  // open: cin, cout
  Adder #(.width(5)) adder_2 (.a(not_2_out), .b(5'b00001), .out(adder_2_out));  // open: cin, cout
  Multiplexer #(.width(10)) multiplexer_3 (.in0(10'h3f3), .in1(adder_1_out), .out(input1), .sel(1'b1));  // open: en
  Multiplexer #(.width(5)) multiplexer_4 (.in0(5'b00011), .in1(adder_2_out), .out(input2), .sel(1'b0));  // open: en
  assign not_4_out = ~register_2_q;  // NOT_Gate not_4, 5 bits wide
  Register #(.width(5)) register_2 (.D(input2), .en(LD_AB), .Q(register_2_q), .clk(C), .clr(RST));
  not not_5 (not_5_out, LD_AB);
  Adder #(.width(5)) adder_3 (.a(not_4_out), .b(5'b00001), .out(adder_3_out));  // open: cin, cout
  D_Flip_Flop d_ff_1 (.clk(C), .D(CHCK), .Q(R0), .reset(RST));  // open: Qn, preset, en
  and and_1 (and_1_out, CT_0, lastOp[0], lastOp[1]);
  Counter #(.width(3), .max('h5)) counter_1 (
    .load(1'b1), .D(3'b101), .count(not_5_out), .Q(counter_1_q), .clk(STEP), .clr(RST));  // open: carry
  Multiplexer #(.width(5)) multiplexer_5 (
    .in0(adder_3_out), .in1(register_2_q), .out(multiplexer_5_out), .sel(Ostatok[4]));  // open: en
  assign not_6_out = ~Chastnoe;  // NOT_Gate not_6, 5 bits wide
  Multiplexer multiplexer_6 (.in0(LD_Ost1), .in1(Ostatok[4]), .out(LD_Ost1_2), .sel(and_1_out));  // open: en
  Adder #(.width(5)) adder_4 (.a(multiplexer_5_out), .b(Ostatok), .out(RGR_INP), .cout(adder_4_cout));  // open: cin
  Adder #(.width(5)) adder_5 (.a(not_6_out), .b(5'b00001), .out(adder_5_out));  // open: cin, cout
  assign not_7_out = ~Chastnoe;  // NOT_Gate not_7, 5 bits wide
  assign not_8_out = ~Ostatok;  // NOT_Gate not_8, 5 bits wide
  assign not_9_out = ~Ostatok;  // NOT_Gate not_9, 5 bits wide
  nor nor_1 (CT_0, counter_1_q[0], counter_1_q[1], counter_1_q[2]);
  Adder #(.width(5)) adder_6 (.a(not_7_out), .b(5'b00001), .out(adder_6_out));  // open: cin, cout
  Adder #(.width(5)) adder_7 (.a(not_8_out), .b(5'b00001), .out(adder_7_out));  // open: cin, cout
  Adder #(.width(5)) adder_8 (.a(not_9_out), .b(5'b00001), .out(adder_8_out));  // open: cin, cout
  Multiplexer #(.width(5)) multiplexer_7 (.in0(RGR_INP), .in1(input1[9:5]), .out(Ost), .sel(LD_Ost2));  // open: en
  Multiplexer #(.select(2), .width(10)) multiplexer_8 (
    .in0({Ostatok, Chastnoe}), .in1({Ostatok, adder_5_out}), .in2({adder_7_out, adder_6_out}),
    .in3({adder_8_out, Chastnoe}), .out({OstatokOtv, ChastnoeOtv}), .sel(2'b10));  // open: en

  // Other names for the same wires on the sheet: znak = Ostatok[4]

  // Notes on the sheet:
  //   C
  //   Частное
  //   Остаток
  //   contents of rom_1 (hex, n*v repeats v):
  //   44e c04 700
  //   contents of rom_2 (hex, n*v repeats v):
  //   11 820 845 c81
  //   S
  //   H
endmodule
